# Fritzing sketch IRlegocar (saved by Fritzing 0.9.3b)

parts:
  Componente1 = Arduino Uno (Rev3)
  IR1 = TSOP312.., 314.. [package=THT]
  J1 = Basic Servo
  Lego_battery = Battery block 9V
  IC1 = H-Bridge [package=THT]
  Lego_DC_motor = DC Motor

nets:
  N1: Componente1.D9_PWM, J1.pulse
  N2: Componente1.D11_PWM/MOSI, IR1.Data
  N3: Componente1.D5_PWM, IC1.1A
  N4: Componente1.D6_PWM, IC1.2A
  N5: Componente1.5V, IR1.Vs
  GND: Componente1.GND, IR1.GND
  GND_2: J1.gnd, IC1.GND3
  N6: J1.vcc, IC1.VCC1
  N7: Lego_battery.-, IC1.GND1
  N8: Lego_battery.+, IC1.VCC2
  N9: IC1.1Y, Lego_DC_motor.pin_2
  N10: IC1.2Y, Lego_DC_motor.pin_1
