# Fritzing sketch IRremote (saved by Fritzing 0.9.3b)
breadboards: 1

parts:
  R1 = Resistor [tolerance=±5% resistance=100 package=THT]
  part = LED - 5mm [color="Green (560nm)" package="5 mm [THT]"]
  part_2 = LED - 5mm [color="Infrared (940nm)" package="5 mm [THT]"]
  R2 = Resistor [tolerance=±5% resistance=220 package=THT]
  Nunchuk1 = Nunchuk [part_number=1]
  Componente1 = Arduino Uno (Rev3)

nets:
  N1: R1.Pin_0, part_2.anode
  N2: R1.Pin_1, Componente1.D3_PWM
  GND: part.cathode, part_2.cathode, Nunchuk1.GND, Componente1.GND
  N3: part.anode, R2.Pin_0
  N4: R2.Pin_1, Componente1.D13/SCK
  N5: Nunchuk1.A4, Componente1.A4/SDA
  VCC: Nunchuk1.VCC, Componente1.3V3
  N6: Nunchuk1.A5, Componente1.A5/SCL

custom parts:
  Nunchuk: Wii nunchuk connector
